// Digital circuit canis.dig as structural Verilog
module canis (
  input  clk
);

  wire decoder_1_str, decoder_1_uimm, decoder_1_we;
  wire [2:0] decoder_1_dsrc, decoder_1_ra, decoder_1_rb, decoder_1_rw;
  wire [3:0] decoder_1_aluo;
  wire [15:0] add_1_s, addressspace_1_d, addressspace_1_i, alu_1_cry, alu_1_out, decoder_1_imm,
       multiplexer_1_out, multiplexer_2_out, PC_q, Registers_da, Registers_db;

  Register #(.Bits(16), .generic("this.Bits=int(args.bits);")) PC (.D(add_1_s), .C(clk), .en(1'b1), .Q(PC_q));
  Add #(.Bits(16)) add_1 (.a(PC_q), .b(16'h1), .c_i(1'b0), .s(add_1_s));  // open: c_o
  addressSpace addressspace_1 (
    .C(clk), .Ia(PC_q), .Da(alu_1_out), .Din(Registers_db), .str(decoder_1_str), .I(addressspace_1_i),
    .D(addressspace_1_d));
  decoder decoder_1 (
    .C(clk), .I(addressspace_1_i), .imm(decoder_1_imm), .uImm(decoder_1_uimm), .ALUo(decoder_1_aluo),
    .Dsrc(decoder_1_dsrc), .we(decoder_1_we), .Rw(decoder_1_rw), .Ra(decoder_1_ra), .Rb(decoder_1_rb),
    .str(decoder_1_str));
  Multiplexer #(.Selector_Bits(3), .Bits(16)) multiplexer_1 (
    .sel(decoder_1_dsrc), .in_0(alu_1_out), .in_1(multiplexer_2_out), .in_2(addressspace_1_d), .in_3(PC_q),
    .in_4(alu_1_cry), .in_5({16{1'b0}}), .in_6({16{1'b0}}), .in_7({16{1'b0}}), .out(multiplexer_1_out));
  RegisterFile #(.AddrBits(3), .Bits(16)) Registers (
    .Din(multiplexer_1_out), .we(decoder_1_we), .Rw(decoder_1_rw), .C(clk), .Ra(decoder_1_ra),
    .Rb(decoder_1_rb), .Da(Registers_da), .Db(Registers_db));
  Multiplexer #(.Bits(16)) multiplexer_2 (
    .sel(decoder_1_uimm), .in_0(Registers_db), .in_1(decoder_1_imm), .out(multiplexer_2_out));
  alu alu_1 (.C(clk), .a(Registers_da), .b(multiplexer_2_out), .op(decoder_1_aluo), .out(alu_1_out), .cry(alu_1_cry));
endmodule
