// Digital circuit decoder.dig as structural Verilog
module decoder (
  input  C,
  input  [15:0] I,
  output [15:0] imm,
  output uImm,
  output [3:0] ALUo,
  output [2:0] Dsrc,
  output we,
  output [2:0] Rw,
  output [2:0] Ra,
  output [2:0] Rb,
  output str
);

  wire and_1_out, enable_ALU, imm_2_0__select, imm_5_3__select, write_register_select;
  wire [1:0] imm_size;
  wire [2:0] fun3, multiplexer_2_out, rd;
  wire [3:0] etypebuffer_1_iext;
  wire [4:0] multiplexer_1_out;
  wire [5:3] multiplexer_3_out;
  wire [13:12] undriven;
  wire [15:0] bitextender_1_out, bitextender_2_out, bitextender_3_out;
  wire [31:16] etypebuffer_1_iext_2;

  eTypeBuffer etypebuffer_1 (.I(I), .C(C), .Iext({etypebuffer_1_iext_2, Ra, fun3, Rb, rd, etypebuffer_1_iext}));
  and and_1 (and_1_out, etypebuffer_1_iext[3], etypebuffer_1_iext[2], etypebuffer_1_iext[1], etypebuffer_1_iext[0]);
  Multiplexer #(.Bits(5)) multiplexer_1 (
    .sel(and_1_out), .in_0({1'b0, etypebuffer_1_iext}), .in_1({2'b10, Ra}), .out(multiplexer_1_out));
  ROM #(.AddrBits(5), .Bits(12)) OpcodeLUT (
    .A(multiplexer_1_out), .sel(1'b1),
    .D({Dsrc, write_register_select, we, uImm, ALUo[3], enable_ALU, imm_size, imm_5_3__select, imm_2_0__select}));
  Multiplexer #(.Bits(3)) multiplexer_2 (.sel(imm_2_0__select), .in_0(rd), .in_1(Rb), .out(multiplexer_2_out));
  Multiplexer #(.Bits(3)) multiplexer_3 (.sel(imm_5_3__select), .in_0(Rb), .in_1(fun3), .out(multiplexer_3_out));
  BitExtender #(.inputBits(3)) bitextender_1 (.in(multiplexer_2_out), .out(bitextender_1_out));
  BitExtender #(.inputBits(6)) bitextender_2 (.in({multiplexer_3_out, multiplexer_2_out}), .out(bitextender_2_out));
  BitExtender #(.inputBits(9)) bitextender_3 (.in({Ra, multiplexer_3_out, multiplexer_2_out}), .out(bitextender_3_out));
  Multiplexer #(.Selector_Bits(2), .Bits(16)) multiplexer_4 (
    .sel(imm_size), .in_0(bitextender_1_out), .in_1(bitextender_2_out), .in_2(bitextender_3_out),
    .in_3(etypebuffer_1_iext_2), .out(imm));
  Multiplexer #(.Bits(3)) multiplexer_5 (.sel(write_register_select), .in_0(rd), .in_1(Ra), .out(Rw));
  Multiplexer #(.Bits(3)) multiplexer_6 (.sel(enable_ALU), .in_0(3'b000), .in_1(fun3), .out(ALUo[2:0]));
  // Pins of 12 and 14 bits meet at {undriven, Dsrc, write_register_select, we, uImm, ALUo[3], enable_ALU, imm_size, imm_5_3__select, imm_2_0__select}

  // Other names for the same wires on the sheet: ALU_carry = ALUo[3]; ALU_use_imm = uImm; enable_write = we;
  //   write_register_source[2:0] = Dsrc; rs2[2:0] = Rb; rs1[2:0] = Ra; clock = C

  // Notes on the sheet:
  //   OpcodeLUT bit format
  //   0 -> Read imm[2:0] from instr[9:7], else from instr[6:4]
  //   1 -> Read imm[5:3] from instr[12:10], else from instr[9:7]
  //   2-3 -> 0: Extend imm from 3 bits, 1: Extend imm from 6 bits, 2: Extend imm from 9 bits, 3: Use instr[31:15] as imm
  //   4 -> Use fun3 as ALUo, else 0
  //   5 -> Enable ALU carry
  //   6 -> Use immediate as ALUb, else rs2
  //   7 -> Enable register write
  //   8 -> Write to rs1, else rd
  //   9-11 -> 0: Write ALU output, 1: Write ALUb, 2: Write Memory, 3: Write PC, 4: Write Carry, 5: Write Timer
  //   contents of OpcodeLUT (hex, n*v repeats v):
  //   90,b0,d1,1d4,dc,2cb,2cc
endmodule
